# Fritzing sketch Sketch (saved by Fritzing 0.9.3b)
breadboards: 1

parts:
  Stromversorgung_Beradboard1 = Stromversorgung Beradboard [package=THT]
  U1 = ESP32S-HiLetgo [part_number=ESP32S-HiLetgo]
  Part1 = Arduino Uno (Rev3) - ICSP
  Part2 = RFID-RC522-v3
  Part3 = RFID-RC522-v3

nets:
  N1: Stromversorgung_Beradboard1.+5_/_+3_Volt_4#13, Part1.VIN
  N2: Stromversorgung_Beradboard1.Ground_1#14, U1.3.3, Part2.3.3V
  GND: Stromversorgung_Beradboard1.Ground_1#15, U1.GND, Part1.GND, Part2.GND
  N3: U1.GPIO17, Part1.D0/RX
  N4: Part1.ICSP_MISO, Part1.D12/MISO, Part2.MISO
  N5: Part1.D8, Part2.SDA
  N6: Part1.D9_PWM, Part2.RST
  N7: Part1.D11_PWM/MOSI, Part2.MOSI
  N8: Part1.D13/SCK, Part2.SCK
  N9: Part1.D7, Part3.SDA

custom parts:
  ESP32S-HiLetgo: HiLetgo ESP-WROOM-32 ESP32 ESP-32S Development Board 2.4GHz Dual-Mode WiFi + Bluetooth Dual Cores Microcontroller The ESP32 integrated with Antenna switches, RF Balun, power amplifiers, low-noise amplifiers, filters, and management modules, and the entire solution occupies the least area of PCB. 2.4 GHz Wi-Fi plus Bluetooth dual-mode chip, with TSMC Ultra-low power consumption 40nm technology,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
  RFID-RC522-v3: A simple China made RFID-RC522 Reader (6x4 cm); do check the pin labels, as this is a MFRC522 based clone.
